// Logisim project Traffic_Light_FSM.circ as structural Verilog: 1 circuit, main circuit main
module main (
  input  Thru_A,
  input  Turn_A,
  input  Thru_B,
  input  Turn_B,
  input  Reset,
  output [2:0] Next_State,
  output [2:0] Current_State
);

  wire and_1_out, and_2_out, and_3_out, and_4_out, and_5_out, CLK_out, not_1_out, not_2_out, not_3_out,
       not_4_out, not_5_out, not_6_out, not_7_out, not_8_out, not_9_out, not_10_out, not_11_out, not_12_out;

  not not_1 (not_1_out, Current_State[2]);
  not not_2 (not_2_out, Current_State[1]);
  not not_3 (not_3_out, Current_State[0]);
  not not_4 (not_4_out, Thru_A);
  not not_5 (not_5_out, Current_State[2]);
  not not_6 (not_6_out, Current_State[0]);
  not not_7 (not_7_out, Turn_A);
  not not_8 (not_8_out, Current_State[1]);
  not not_9 (not_9_out, Current_State[0]);
  not not_10 (not_10_out, Thru_B);
  not not_11 (not_11_out, Current_State[0]);
  not not_12 (not_12_out, Turn_B);
  and and_1 (and_1_out, not_1_out, not_2_out, not_3_out, not_4_out);
  and and_2 (and_2_out, not_5_out, Current_State[1], not_6_out, not_7_out);
  and and_3 (and_3_out, Current_State[2], not_8_out, not_9_out, not_10_out);
  and and_4 (and_4_out, Current_State[2], Current_State[1], not_11_out, not_12_out);
  and and_5 (and_5_out, Current_State[0], Current_State[1]);
  xor xor_1 (Next_State[1], Current_State[0], Current_State[1]);
  or or_1 (Next_State[0], and_1_out, and_2_out, and_3_out, and_4_out);
  xor xor_2 (Next_State[2], Current_State[2], and_5_out);
  Clock CLK (.out(CLK_out));
  D_Flip_Flop d_ff_1 (.D(Next_State[2]), .clk(CLK_out), .Q(Current_State[2]), .reset(Reset));  // open: Qn, preset
  D_Flip_Flop d_ff_2 (.D(Next_State[1]), .clk(CLK_out), .Q(Current_State[1]), .reset(Reset));  // open: Qn, preset
  D_Flip_Flop d_ff_3 (.D(Next_State[0]), .clk(CLK_out), .Q(Current_State[0]), .reset(Reset));  // open: Qn, preset
endmodule
